# Fritzing sketch power-meter (saved by Fritzing 0.9.9b)
circuit board: 8.46667cm x 5.64444cm
breadboards: 1

parts:
  ADS1115 = Arduino Uno (Rev3)
  Pepito = ADS1115
  U2 = 2.5mm Audio Jack [package=stereojack2.5mm_smd]  # not connected

nets:
  5V: ADS1115.5V, Pepito.VDD

notes:
  Ver pinout del SCT013: L=Sleeve,K = Tip

custom parts:
  ADS1115: ADC ADS1115
